// Logisim project mathCPU.circ as structural Verilog: 8 circuits, main circuit ALU
module MAIN (
  input  [3:0] Data,
  input  [2:0] Flag,
  output [3:0] out_3
);

  wire F, R, Reset_out, RUN_out, Set_A_out, Set_B_out, Set_Opcode_out, tunnel, tunnel_t, tunnel_t_t,
       tunnel_t_t_t, W_A, W_B;
  wire [3:0] A, B;
  wire [23:0] Op;

  Hex_Digit_Display hex_digit_display_1 (.value(Data));  // open: dp
  Button Set_A (.out(Set_A_out));
  Button Set_B (.out(Set_B_out));
  Button Set_Opcode (.out(Set_Opcode_out));
  Button RUN (.out(RUN_out));
  Button Reset (.out(Reset_out));
  Hex_Digit_Display hex_digit_display_2 (.value({1'b0, Flag}));  // open: dp
  CPU cpu_1 (
    .Data(Data), .Flags(Flag), .Set_A(Set_A_out), .Set_B(Set_B_out), .Set_Opcode(Set_Opcode_out),
    .Run(RUN_out), .Reset(Reset_out), .Output(out_3), .Program(Op), .State_of_register_A(A),
    .State_of_register_B(B), .Writing_to_register_A(W_A), .Writing_to_register_B(W_B), .Flag(F),
    .Overflow(tunnel_t), .Negative(tunnel_t_t), .Overflow_2(tunnel), .Modulo(tunnel_t_t_t), .Running(R));
  Hex_Digit_Display hex_digit_display_3 (.value(out_3));  // open: dp
  Hex_Digit_Display hex_digit_display_4 (.value(A));  // open: dp
  Hex_Digit_Display hex_digit_display_5 (.value(B));  // open: dp
  LED Writing_to_register_A (.in(W_A));
  LED Writing_to_register_B (.in(W_B));
  LED Overflow (.in(tunnel_t));
  LED Overflow_2 (.in(tunnel));
  LED Negative (.in(tunnel_t_t));
  LED Modulo (.in(tunnel_t_t_t));
  LED u_Flag (.in(F));
  LED Running (.in(R));
  Hex_Digit_Display hex_digit_display_6 (.value(Op[3:0]));  // open: dp
  Hex_Digit_Display hex_digit_display_7 (.value(Op[7:4]));  // open: dp
  Hex_Digit_Display hex_digit_display_8 (.value(Op[11:8]));  // open: dp
  Hex_Digit_Display hex_digit_display_9 (.value(Op[19:16]));  // open: dp
  Hex_Digit_Display hex_digit_display_10 (.value(Op[15:12]));  // open: dp
  Hex_Digit_Display hex_digit_display_11 (.value(Op[23:20]));  // open: dp

  // Notes on the sheet:
  //   Inputs
  //   Output
  //   Controls
  //   Register A
  //   Register B
  //   Program
endmodule

module CPU (
  input  [3:0] Data,
  input  [2:0] Flags,
  input  Set_A,
  input  Set_B,
  input  Set_Opcode,
  input  Run,
  input  Reset,
  output [3:0] Output,
  output [23:0] Program,
  output [3:0] State_of_register_A,
  output [3:0] State_of_register_B,
  output Writing_to_register_A,
  output Writing_to_register_B,
  output Flag,
  output Overflow,
  output Negative,
  output Overflow_2,
  output Modulo,
  output Running
);

  wire and_2_out, and_4_out, and_5_out, clock_1_out, counter_1_carry, not_1_out, not_2_out, not_3_out,
       or_1_out, xor_1_out, xor_2_out, xor_3_out;
  wire [3:0] alu_1_output, controlled_buffer_1_out, controlled_buffer_2_out, multiplexer_1_out, Opcode;

  Clock clock_1 (.out(clock_1_out));
  D_Flip_Flop d_ff_1 (.clk(Run), .D(Run), .Q(Running), .reset(counter_1_carry));  // open: Qn, preset, en
  and and_1 (Writing_to_register_B, Opcode[3], Opcode[2], Opcode[1], Opcode[0]);
  not not_1 (not_1_out, Writing_to_register_A);
  assign controlled_buffer_1_out = not_1_out ? Data : 4'bz;  // Controlled_Buffer controlled_buffer_1
  not not_2 (not_2_out, Writing_to_register_B);
  assign controlled_buffer_2_out = not_2_out ? Data : 4'bz;  // Controlled_Buffer controlled_buffer_2
  and and_2 (and_2_out, Running, clock_1_out);
  not not_3 (not_3_out, Opcode[0]);
  and and_3 (Writing_to_register_A, Opcode[3], Opcode[2], Opcode[1], not_3_out);
  assign controlled_buffer_1_out = Writing_to_register_A ? Output : 4'bz;  // Controlled_Buffer controlled_buffer_3
  and and_4 (and_4_out, Writing_to_register_A, clock_1_out);
  assign controlled_buffer_2_out = Writing_to_register_B ? Output : 4'bz;  // Controlled_Buffer controlled_buffer_4
  and and_5 (and_5_out, Writing_to_register_B, clock_1_out);
  Multiplexer #(.width(4), .enable("false")) multiplexer_1 (
    .in0(Data), .in1(4'b0000), .out(multiplexer_1_out), .sel(Running));
  Shift_Register #(.width(4), .length(6)) shift_register_1 (
    .in(multiplexer_1_out), .clk(xor_1_out), .out(Opcode), .clr(Reset), .q0(Program[23:20]),
    .q1(Program[19:16]), .q2(Program[15:12]), .q3(Program[11:8]), .q4(Program[7:4]), .q5(Program[3:0]));  // open: shift, load, d0, d1, d2, d3, d4, d5
  xor xor_1 (xor_1_out, and_2_out, Set_Opcode);
  or or_1 (or_1_out, Reset, counter_1_carry);
  Register #(.width(4)) register_1 (
    .D(controlled_buffer_1_out), .Q(State_of_register_A), .clk(xor_2_out), .clr(Reset));  // open: en
  xor xor_2 (xor_2_out, and_4_out, Set_A);
  Register #(.width(4)) register_2 (
    .D(controlled_buffer_2_out), .Q(State_of_register_B), .clk(xor_3_out), .clr(Reset));  // open: en
  xor xor_3 (xor_3_out, and_5_out, Set_B);
  Counter #(.width(3), .max('h5)) counter_1 (
    .carry(counter_1_carry), .clk(and_2_out), .clr(or_1_out));  // open: load, D, count, Q
  ALU alu_1 (
    .Cin(1'b0), .InputA(State_of_register_A), .InputB(State_of_register_B), .Opcode(Opcode), .Flags(Flags),
    .Output(alu_1_output), .Negative(Negative), .plus_Overflow(Overflow), .Overflow(Overflow_2),
    .Modulo(Modulo), .Flag(Flag));
  Register #(.width(4)) register_3 (.D(alu_1_output), .Q(Output), .clk(clock_1_out), .clr(Reset));  // open: en

  // Other names for the same wires on the sheet: F = Flag; R = Running; S_A[3:0] = State_of_register_A;
  //   S_B[3:0] = State_of_register_B; tunnel = Overflow_2; tunnel_t = Overflow; tunnel_t_t = Negative;
  //   tunnel_t_t_t = Modulo; W_A = Writing_to_register_A; W_B = Writing_to_register_B
endmodule

module ALU (
  input  Cin,
  input  [3:0] InputA,
  input  [3:0] InputB,
  input  [3:0] Opcode,
  input  [2:0] Flags,
  output [3:0] Output,
  output Negative,
  output plus_Overflow,
  output Overflow,
  output Modulo,
  output Flag
);

  wire comparator_1_eq, comparator_1_gt, comparator_1_lt, not_3_out, or_2_out, or_3_out;
  wire [3:0] and_1_out, divider_1_out, Modulo_t, n4_bit_adder_1_output, n4_bit_multiplier_1_output,
       n4_bit_subtractor_1_output, not_1_out, not_2_out, or_1_out, Overflow_t, shifter_1_out, shifter_2_out;

  _4_bit_Adder u_4_bit_adder_1 (
    .Cin(Cin), .InputA(InputA), .InputB(InputB), .Output(n4_bit_adder_1_output), .Cout(plus_Overflow));
  _4_bit_Subtractor u_4_bit_subtractor_1 (
    .InputA(InputA), .InputB(InputB), .Output(n4_bit_subtractor_1_output), .Negative(Negative));
  _4_bit_Multiplier u_4_bit_multiplier_1 (
    .in_1(Cin), .InputA(InputA), .InputB(InputB), .Output(n4_bit_multiplier_1_output), .Overflow(Overflow_t));
  Divider #(.width(4)) divider_1 (.a(InputA), .b(InputB), .out(divider_1_out), .rem(Modulo_t));  // open: upper
  assign not_1_out = ~InputA;  // NOT_Gate not_1, 4 bits wide
  assign not_2_out = ~InputB;  // NOT_Gate not_2, 4 bits wide
  Shifter #(.width(4), .shift("lr")) shifter_1 (.in(InputA), .\dist (InputB[1:0]), .out(shifter_1_out));
  Shifter #(.width(4)) shifter_2 (.in(InputB), .\dist (InputB[1:0]), .out(shifter_2_out));
  assign and_1_out = InputA & InputB;  // AND_Gate and_1, 4 bits wide
  assign or_1_out = InputA | InputB;  // OR_Gate or_1, 4 bits wide
  Comparator #(.width(4), .mode("unsigned")) comparator_1 (
    .a(InputA), .b(InputB), .gt(comparator_1_gt), .eq(comparator_1_eq), .lt(comparator_1_lt));
  or or_2 (or_2_out, comparator_1_eq, comparator_1_gt);
  or or_3 (or_3_out, comparator_1_lt, comparator_1_eq);
  Multiplexer #(.select(3), .enable("false")) multiplexer_1 (
    .in0(comparator_1_gt), .in1(comparator_1_eq), .in2(comparator_1_lt), .in3(or_2_out), .in4(or_3_out),
    .in5(not_3_out), .out(Flag), .sel(Flags));  // open: in6, in7
  not not_3 (not_3_out, comparator_1_eq);
  Multiplexer #(.select(4), .width(4), .enable("false")) multiplexer_2 (
    .in0(n4_bit_adder_1_output), .in1(n4_bit_subtractor_1_output), .in2(n4_bit_multiplier_1_output),
    .in3(Overflow_t), .in4(divider_1_out), .in5(Modulo_t), .in6(not_1_out), .in7(not_2_out),
    .in8(shifter_1_out), .in9(shifter_2_out), .in10(and_1_out), .in11(or_1_out), .in12(InputA),
    .in13(InputB), .out(Output), .sel(Opcode));  // open: in14, in15
  or or_4 (Overflow, Overflow_t[3], Overflow_t[2], Overflow_t[1], Overflow_t[0]);
  or or_5 (Modulo, Modulo_t[3], Modulo_t[2], Modulo_t[1], Modulo_t[0]);
endmodule

module _4_bit_Multiplier (
  input  in_1,
  input  [3:0] InputA,
  input  [3:0] InputB,
  output [3:0] Output,
  output [3:0] Overflow
);

  wire [2:0] and_2_out;
  wire [3:0] and_5_out, and_9_out, and_13_out, n4_bit_adder_1_cout, n4_bit_adder_2_cout;

  and and_1 (Output[0], InputA[0], InputB[0]);
  and and_2 (and_2_out[0], InputA[1], InputB[0]);
  and and_3 (and_2_out[1], InputA[2], InputB[0]);
  and and_4 (and_2_out[2], InputA[3], InputB[0]);
  and and_5 (and_5_out[0], InputA[0], InputB[1]);
  and and_6 (and_5_out[1], InputA[1], InputB[1]);
  and and_7 (and_5_out[2], InputA[2], InputB[1]);
  and and_8 (and_5_out[3], InputA[3], InputB[1]);
  and and_9 (and_9_out[0], InputA[0], InputB[2]);
  and and_10 (and_9_out[1], InputA[1], InputB[2]);
  and and_11 (and_9_out[2], InputA[2], InputB[2]);
  and and_12 (and_9_out[3], InputA[3], InputB[2]);
  and and_13 (and_13_out[0], InputA[0], InputB[3]);
  and and_14 (and_13_out[1], InputA[1], InputB[3]);
  and and_15 (and_13_out[2], InputA[2], InputB[3]);
  and and_16 (and_13_out[3], InputA[3], InputB[3]);
  _4_bit_Adder u_4_bit_adder_1 (
    .Cin(in_1), .InputA({in_1, and_2_out}), .InputB(and_5_out),
    .Output({n4_bit_adder_1_cout[2:0], Output[1]}), .Cout(n4_bit_adder_1_cout[3]));
  _4_bit_Adder u_4_bit_adder_2 (
    .Cin(in_1), .InputA(n4_bit_adder_1_cout), .InputB(and_9_out),
    .Output({n4_bit_adder_2_cout[2:0], Output[2]}), .Cout(n4_bit_adder_2_cout[3]));
  _4_bit_Adder u_4_bit_adder_3 (
    .Cin(in_1), .InputA(n4_bit_adder_2_cout), .InputB(and_13_out), .Output({Overflow[2:0], Output[3]}),
    .Cout(Overflow[3]));
endmodule

module _4_bit_Subtractor (
  input  [3:0] InputA,
  input  [3:0] InputB,
  output [3:0] Output,
  output Negative
);

  wire adder_1_carry, adder_2_carry, adder_3_carry, xor_1_out, xor_2_out, xor_3_out, xor_4_out;

  xor xor_1 (xor_1_out, 1'b1, InputB[0]);
  xor xor_2 (xor_2_out, 1'b1, InputB[1]);
  xor xor_3 (xor_3_out, 1'b1, InputB[2]);
  xor xor_4 (xor_4_out, 1'b1, InputB[3]);
  Comparator #(.width(4), .mode("unsigned")) comparator_1 (.a(InputA), .b(InputB), .lt(Negative));  // open: gt, eq
  Adder adder_1 (.A(1'b1), .B(InputA[0]), .C(xor_1_out), .Sum(Output[0]), .Carry(adder_1_carry));
  Adder adder_2 (.A(adder_1_carry), .B(InputA[1]), .C(xor_2_out), .Sum(Output[1]), .Carry(adder_2_carry));
  Adder adder_3 (.A(adder_2_carry), .B(InputA[2]), .C(xor_3_out), .Sum(Output[2]), .Carry(adder_3_carry));
  Adder adder_4 (.A(adder_3_carry), .B(InputA[3]), .C(xor_4_out), .Sum(Output[3]));  // open: Carry
endmodule

module _4_bit_Adder (
  input  Cin,
  input  [3:0] InputA,
  input  [3:0] InputB,
  output [3:0] Output,
  output Cout
);

  wire adder_1_carry, adder_2_carry, adder_3_carry;

  Adder adder_1 (.A(InputA[0]), .B(InputB[0]), .C(Cin), .Sum(Output[0]), .Carry(adder_1_carry));
  Adder adder_2 (.A(adder_1_carry), .B(InputA[1]), .C(InputB[1]), .Sum(Output[1]), .Carry(adder_2_carry));
  Adder adder_3 (.A(adder_2_carry), .B(InputA[2]), .C(InputB[2]), .Sum(Output[2]), .Carry(adder_3_carry));
  Adder adder_4 (.A(adder_3_carry), .B(InputA[3]), .C(InputB[3]), .Sum(Output[3]), .Carry(Cout));
endmodule

module Subtractor (
  input  A,
  input  B,
  input  C,
  output Output,
  output Borrow
);

  wire and_1_out, and_2_out, and_3_out, not_1_out, or_1_out;

  not not_1 (not_1_out, A);
  and and_1 (and_1_out, B, C);
  and and_2 (and_2_out, not_1_out, C);
  ExactlyOne xor_1 (.out(Output), .in0(A), .in1(B), .in2(C));
  or or_1 (or_1_out, and_1_out, and_2_out);
  and and_3 (and_3_out, not_1_out, B);
  or or_2 (Borrow, or_1_out, and_3_out);
endmodule

module Adder (
  input  A,
  input  B,
  input  C,
  output Sum,
  output Carry
);

  wire and_1_out, and_2_out, xor_1_out;

  xor xor_1 (xor_1_out, A, B);
  xor xor_2 (Sum, xor_1_out, C);
  and and_1 (and_1_out, C, xor_1_out);
  and and_2 (and_2_out, A, B);
  or or_1 (Carry, and_1_out, and_2_out);
endmodule
